// Logisim project Vertabrate32bit.circ as structural Verilog
module Vertebrate32 (
);

  main main_1 ();
endmodule

module RegisterBank32 (
  input  [31:0] DOUT1,
  input  [31:0] DOUT2,
  input  [2:0] RegSelect,
  input  [31:0] DOUT3,
  input  [31:0] DOUT4,
  input  [31:0] DOUT5,
  input  RegLoad,
  input  [31:0] DOUT6,
  input  [31:0] Data_In,
  input  [31:0] DOUT7,
  input  [31:0] DOUT8
);

  wire and_1_out, and_2_out, and_3_out, and_4_out, and_5_out, and_6_out, and_7_out, and_8_out,
       decoder_1_out0, decoder_1_out1, decoder_1_out2, decoder_1_out3, decoder_1_out4, decoder_1_out5,
       decoder_1_out6, decoder_1_out7;

  Decoder #(.select(3)) decoder_1 (
    .out0(decoder_1_out0), .out1(decoder_1_out1), .out2(decoder_1_out2), .out3(decoder_1_out3),
    .out4(decoder_1_out4), .out5(decoder_1_out5), .out6(decoder_1_out6), .out7(decoder_1_out7),
    .sel(RegSelect));  // open: en
  and and_1 (and_1_out, decoder_1_out0, RegLoad);
  and and_2 (and_2_out, decoder_1_out1, RegLoad);
  and and_3 (and_3_out, decoder_1_out2, RegLoad);
  and and_4 (and_4_out, decoder_1_out3, RegLoad);
  and and_5 (and_5_out, decoder_1_out4, RegLoad);
  and and_6 (and_6_out, decoder_1_out5, RegLoad);
  and and_7 (and_7_out, decoder_1_out6, RegLoad);
  and and_8 (and_8_out, decoder_1_out7, RegLoad);
  Register #(.width(32)) Register_0 (.D(Data_In), .en(and_1_out), .Q(DOUT1));  // open: clk, clr
  Register #(.width(32)) Register_1 (.D(Data_In), .en(and_2_out), .Q(DOUT2));  // open: clk, clr
  Register #(.width(32)) Register_2 (.D(Data_In), .en(and_3_out), .Q(DOUT3));  // open: clk, clr
  Register #(.width(32)) Register_3 (.D(Data_In), .en(and_4_out), .Q(DOUT4));  // open: clk, clr
  Register #(.width(32)) Register_4 (.D(Data_In), .en(and_5_out), .Q(DOUT5));  // open: clk, clr
  Register #(.width(32)) Register_5 (.D(Data_In), .en(and_6_out), .Q(DOUT6));  // open: clk, clr
  Register #(.width(32)) Register_6 (.D(Data_In), .en(and_7_out), .Q(DOUT7));  // open: clk, clr
  Register #(.width(32)) Register_7 (.D(Data_In), .en(and_8_out), .Q(DOUT8));  // open: clk, clr
endmodule
